// Logisim project 74HC_library.circ as structural Verilog: 2 circuits, main circuit main
module main (
);

  CD74HC173_quad_D_type_flip_flop cd74hc173_quad_d_type_flip_flop_1 ();  // open: Q0, Q1, Q2, Q3, not_OE2, not_E1, not_E2, CP, MR, D0, not_OE1, D1, D2, D3
endmodule

module CD74HC173_quad_D_type_flip_flop (
  input  not_OE1,
  input  not_OE2,
  input  not_E1,
  input  not_E2,
  input  CP,
  input  MR,
  input  D0,
  input  D1,
  input  D2,
  input  D3,
  output Q0,
  output Q1,
  output Q2,
  output Q3
);

  wire and_1_out, and_2_out, and_3_out, and_4_out, and_5_out, and_6_out, and_7_out, and_8_out, buffer_1_out,
       buffer_2_out, buffer_3_out, buffer_4_out, buffer_7_out, buffer_8_out, buffer_9_out, buffer_10_out,
       CP_t, d_ff_1_q, d_ff_2_q, d_ff_3_q, d_ff_4_q, E, MR_t, not_E, OE, or_2_out, or_3_out, or_4_out,
       or_5_out;

  buf buffer_1 (buffer_1_out, not_OE1);
  buf buffer_2 (buffer_2_out, not_OE2);
  buf buffer_3 (buffer_3_out, not_E1);
  buf buffer_4 (buffer_4_out, not_E2);
  buf buffer_5 (CP_t, CP);
  buf buffer_6 (MR_t, MR);
  buf buffer_7 (buffer_7_out, D0);
  buf buffer_8 (buffer_8_out, D1);
  buf buffer_9 (buffer_9_out, D2);
  buf buffer_10 (buffer_10_out, D3);
  nor nor_1 (OE, buffer_1_out, buffer_2_out);
  or or_1 (E, buffer_3_out, buffer_4_out);
  not not_1 (not_E, E);
  and and_1 (and_1_out, d_ff_1_q, E);
  or or_2 (or_2_out, and_1_out, and_2_out);
  and and_2 (and_2_out, not_E, buffer_7_out);
  and and_3 (and_3_out, d_ff_2_q, E);
  or or_3 (or_3_out, and_3_out, and_4_out);
  and and_4 (and_4_out, not_E, buffer_8_out);
  and and_5 (and_5_out, d_ff_3_q, E);
  and and_6 (and_6_out, not_E, buffer_9_out);
  and and_7 (and_7_out, d_ff_4_q, E);
  and and_8 (and_8_out, not_E, buffer_10_out);
  D_Flip_Flop d_ff_1 (.D(or_2_out), .clk(CP_t), .Q(d_ff_1_q), .reset(MR_t));  // open: Qn, preset
  D_Flip_Flop d_ff_2 (.D(or_3_out), .clk(CP_t), .Q(d_ff_2_q), .reset(MR_t));  // open: Qn, preset
  D_Flip_Flop d_ff_3 (.D(or_4_out), .clk(CP_t), .Q(d_ff_3_q), .reset(MR_t));  // open: Qn, preset
  or or_4 (or_4_out, and_5_out, and_6_out);
  D_Flip_Flop d_ff_4 (.D(or_5_out), .clk(CP_t), .Q(d_ff_4_q), .reset(MR_t));  // open: Qn, preset
  or or_5 (or_5_out, and_7_out, and_8_out);
  assign Q0 = OE ? d_ff_1_q : 1'bz;  // Controlled_Buffer controlled_buffer_1
  assign Q1 = OE ? d_ff_2_q : 1'bz;  // Controlled_Buffer controlled_buffer_2
  assign Q2 = OE ? d_ff_3_q : 1'bz;  // Controlled_Buffer controlled_buffer_3
  assign Q3 = OE ? d_ff_4_q : 1'bz;  // Controlled_Buffer controlled_buffer_4
endmodule
