// Logisim project 8_bit_CPU.circ as structural Verilog
module NOT_gate (
  input  in_1,
  output out_2
);

  Transistor transistor_1 (.in(1'b1), .out(out_2), .gate(in_1));
  Transistor #(.\type ("n")) transistor_2 (.in(1'b0), .out(out_2), .gate(in_1));

  // Notes on the sheet:
  //   NOT gate
endmodule

module NAND_gate (
  input  in_1,
  input  A,
  input  in_3,
  input  B,
  output out_5,
  output Q
);

  wire B_t, transistor_4_out, transistor_7_out;

  Transistor transistor_1 (.in(1'b1), .out(out_5), .gate(in_1));
  Transistor transistor_2 (.in(1'b1), .out(out_5), .gate(in_3));
  Transistor #(.\type ("n")) transistor_3 (.in(transistor_4_out), .out(out_5), .gate(in_3));
  Transistor #(.\type ("n")) transistor_4 (.in(1'b0), .out(transistor_4_out), .gate(in_1));
  Transistor transistor_5 (.in(1'b1), .out(Q), .gate(A));
  Transistor #(.\type ("n")) transistor_6 (.in(transistor_7_out), .out(Q), .gate(A));
  Transistor #(.\type ("n")) transistor_7 (.in(1'b0), .out(transistor_7_out), .gate(B));
  Transistor transistor_8 (.in(1'b1), .out(Q), .gate(B_t));

  // Notes on the sheet:
  //   NAND gate (2NMOS, 2PMOS)
endmodule

module NOR_gate (
  input  in_1,
  input  in_2,
  output out_3
);

  wire transistor_1_out;

  Transistor transistor_1 (.in(1'b1), .out(transistor_1_out), .gate(in_2));
  Transistor transistor_2 (.in(transistor_1_out), .out(out_3), .gate(in_1));
  Transistor #(.\type ("n")) transistor_3 (.in(1'b0), .out(out_3), .gate(in_1));
  Transistor #(.\type ("n")) transistor_4 (.in(1'b0), .out(out_3), .gate(in_2));

  // Notes on the sheet:
  //   NOR gate (2NMOS, 2PMOS)
endmodule

module SR_latch_active_low (
  input  S,
  input  R,
  output Q,
  output not_Q
);

  nand nand_1 (Q, S, not_Q);
  nand nand_2 (not_Q, Q, R);

  // Notes on the sheet:
  //   Active LOW SR latch
endmodule

module MEM_1 (
  input  input_value,
  input  set,
  output output_value
);

  wire nand_1_out, nand_2_out;

  nand nand_1 (nand_1_out, input_value, set);
  nand nand_2 (nand_2_out, nand_1_out, set);
  SR_latch_active_low sr_latch_active_low_1 (.Q(output_value), .R(nand_2_out), .S(nand_1_out));  // open: not_Q

  // Notes on the sheet:
  //   1 bit memory
endmodule

module D_flip_flop (
  input  S,
  input  input_value,
  input  set,
  input  R,
  output Q
);

  nand nand_1 (S, input_value, set);
  nand nand_2 (R, S, set);
  SR_latch_active_low sr_latch_active_low_1 (.Q(Q), .R(R), .S(S));  // open: not_Q
endmodule

module master_slave_D_flip_flop (
  input  D,
  input  clk,
  output Q
);

  wire d_flip_flop_1_q, not_1_out;

  not not_1 (not_1_out, clk);
  D_flip_flop d_flip_flop_1 (.S(D), .input_value(not_1_out), .Q(d_flip_flop_1_q));  // open: set, R
  D_flip_flop d_flip_flop_2 (.S(d_flip_flop_1_q), .input_value(clk), .Q(Q));  // open: set, R
endmodule

module D_flip_flop_rising_edge (
  input  in_1,
  input  in_2,
  input  in_3,
  output out_4,
  output out_5,
  output out_6
);

  wire clock_1_out, d_flip_flop_1_q, nand_1_out, nand_2_out, nand_3_out, nand_4_out, nand_5_out, nand_6_out,
       not_1_out, not_2_out;

  Clock clock_1 (.out(clock_1_out));
  not not_1 (not_1_out, clock_1_out);
  nand nand_1 (nand_1_out, in_1, not_1_out);
  not not_2 (not_2_out, in_3);
  nand nand_2 (nand_2_out, not_1_out, nand_1_out);
  nand nand_3 (nand_3_out, nand_1_out, nand_4_out);
  nand nand_4 (nand_4_out, nand_3_out, nand_2_out);
  D_flip_flop d_flip_flop_1 (.S(in_2), .input_value(in_3), .Q(d_flip_flop_1_q));  // open: set, R
  nand nand_5 (nand_5_out, nand_3_out, clock_1_out);
  nand nand_6 (nand_6_out, nand_4_out, clock_1_out);
  nand nand_7 (out_4, nand_5_out, out_5);
  nand nand_8 (out_5, out_4, nand_6_out);
  D_flip_flop d_flip_flop_2 (.S(d_flip_flop_1_q), .input_value(not_2_out), .Q(out_6));  // open: set, R
endmodule

module MEM_8 (
  input  [7:0] input_value,
  input  set,
  output [7:0] output_value
);

  MEM_1 mem_1_1 (.output_value(output_value[0]), .set(set), .input_value(input_value[0]));
  MEM_1 mem_1_2 (.output_value(output_value[1]), .set(set), .input_value(input_value[1]));
  MEM_1 mem_1_3 (.output_value(output_value[2]), .set(set), .input_value(input_value[2]));
  MEM_1 mem_1_4 (.output_value(output_value[3]), .set(set), .input_value(input_value[3]));
  MEM_1 mem_1_5 (.output_value(output_value[4]), .set(set), .input_value(input_value[4]));
  MEM_1 mem_1_6 (.output_value(output_value[5]), .set(set), .input_value(input_value[5]));
  MEM_1 mem_1_7 (.output_value(output_value[6]), .set(set), .input_value(input_value[6]));
  MEM_1 mem_1_8 (.output_value(output_value[7]), .set(set), .input_value(input_value[7]));

  // Notes on the sheet:
  //   1 byte memory
endmodule

module REGISTER_8 (
  input  [7:0] input_value,
  input  set,
  input  enable,
  output [7:0] stored_value,
  output [7:0] output_value
);

  assign output_value = enable ? stored_value : 8'bz;  // Controlled_Buffer controlled_buffer_1
  MEM_8 mem_8_1 (.output_value(stored_value), .set(set), .input_value(input_value));

  // Notes on the sheet:
  //   1 byte register
endmodule

module REG_ACCUMULATOR (
  input  [7:0] input_value,
  input  set,
  input  enable,
  output [7:0] output_value,
  output [7:0] stored_value
);

  REGISTER_8 register_8_1 (
    .stored_value(stored_value), .output_value(output_value), .input_value(input_value), .set(set),
    .enable(enable));
endmodule

module REG_TMP (
  input  [7:0] input_value,
  input  set,
  output [7:0] output_value
);

  MEM_8 mem_8_1 (.output_value(output_value), .set(set), .input_value(input_value));
endmodule

module DECODER_3x8 (
  input  [2:0] in_1,
  output start,
  output out_3,
  output out_4,
  output out_5,
  output out_6,
  output out_7,
  output out_8,
  output finish
);

  wire not_1_out, not_2_out, not_3_out;

  not not_1 (not_1_out, in_1[2]);
  not not_2 (not_2_out, in_1[1]);
  not not_3 (not_3_out, in_1[0]);
  and and_1 (start, not_3_out, not_2_out, not_1_out);
  and and_2 (out_3, in_1[0], not_2_out, not_1_out);
  and and_3 (out_4, not_3_out, in_1[1], not_1_out);
  and and_4 (out_5, in_1[0], in_1[1], not_1_out);
  and and_5 (out_6, not_3_out, not_2_out, in_1[2]);
  and and_6 (out_7, in_1[0], not_2_out, in_1[2]);
  and and_7 (out_8, not_3_out, in_1[1], in_1[2]);
  and and_8 (finish, in_1[0], in_1[1], in_1[2]);

  // Notes on the sheet:
  //   3x8 decoder
endmodule

module DECODER_4x16 (
  input  [3:0] in_1,
  output start,
  output out_3,
  output out_4,
  output out_5,
  output out_6,
  output out_7,
  output out_8,
  output out_9,
  output out_10,
  output out_11,
  output out_12,
  output out_13,
  output out_14,
  output out_15,
  output out_16,
  output finish
);

  wire not_1_out, not_2_out, not_3_out, not_4_out;

  not not_1 (not_1_out, in_1[3]);
  not not_2 (not_2_out, in_1[2]);
  not not_3 (not_3_out, in_1[1]);
  not not_4 (not_4_out, in_1[0]);
  and and_1 (start, not_4_out, not_3_out, not_2_out, not_1_out);
  and and_2 (out_3, in_1[0], not_3_out, not_2_out, not_1_out);
  and and_3 (out_4, not_4_out, in_1[1], not_2_out, not_1_out);
  and and_4 (out_5, in_1[0], in_1[1], not_2_out, not_1_out);
  and and_5 (out_6, not_4_out, not_3_out, in_1[2], not_1_out);
  and and_6 (out_7, in_1[0], not_3_out, in_1[2], not_1_out);
  and and_7 (out_8, not_4_out, in_1[1], in_1[2], not_1_out);
  and and_8 (out_9, in_1[0], in_1[1], in_1[2], not_1_out);
  and and_9 (out_10, not_4_out, not_3_out, not_2_out, in_1[3]);
  and and_10 (out_11, in_1[0], not_3_out, not_2_out, in_1[3]);
  and and_11 (out_12, not_4_out, in_1[1], not_2_out, in_1[3]);
  and and_12 (out_13, in_1[0], in_1[1], not_2_out, in_1[3]);
  and and_13 (out_14, not_4_out, not_3_out, in_1[2], in_1[3]);
  and and_14 (out_15, in_1[0], not_3_out, in_1[2], in_1[3]);
  and and_15 (out_16, not_4_out, in_1[1], in_1[2], in_1[3]);
  and and_16 (finish, in_1[0], in_1[1], in_1[2], in_1[3]);

  // Notes on the sheet:
  //   4x16 decoder
endmodule

module MEM_CELL (
  input  [7:0] input_value,
  input  reset,
  input  horisontal_address,
  input  vertical_address,
  input  set,
  input  enable,
  output [7:0] output_value,
  output [7:0] stored_value
);

  wire and_1_out, and_2_out, and_3_out, or_1_out;

  and and_1 (and_1_out, horisontal_address, vertical_address);
  and and_2 (and_2_out, and_1_out, set);
  and and_3 (and_3_out, and_1_out, enable);
  or or_1 (or_1_out, reset, and_2_out);
  REGISTER_8 register_8_1 (
    .stored_value(stored_value), .output_value(output_value), .input_value(input_value), .set(or_1_out),
    .enable(and_3_out));

  // Notes on the sheet:
  //   1 byte memory cell
endmodule

module RAM_256 (
  input  [7:0] address,
  input  set,
  input  enable_read,
  input  reset,
  input  [7:0] input_val,
  input  set_value,
  output [7:0] stored_address,
  output [7:0] output_val
);

  wire decoder_4x16_1_finish, decoder_4x16_1_out_3, decoder_4x16_1_out_4, decoder_4x16_1_out_5,
       decoder_4x16_1_out_6, decoder_4x16_1_out_7, decoder_4x16_1_out_8, decoder_4x16_1_out_9,
       decoder_4x16_1_out_10, decoder_4x16_1_out_11, decoder_4x16_1_out_12, decoder_4x16_1_out_13,
       decoder_4x16_1_out_14, decoder_4x16_1_out_15, decoder_4x16_1_out_16, decoder_4x16_1_start,
       decoder_4x16_2_finish, decoder_4x16_2_out_3, decoder_4x16_2_out_4, decoder_4x16_2_out_5,
       decoder_4x16_2_out_6, decoder_4x16_2_out_7, decoder_4x16_2_out_8, decoder_4x16_2_out_9,
       decoder_4x16_2_out_10, decoder_4x16_2_out_11, decoder_4x16_2_out_12, decoder_4x16_2_out_13,
       decoder_4x16_2_out_14, decoder_4x16_2_out_15, decoder_4x16_2_out_16, decoder_4x16_2_start;
  wire [7:0] mem_cell_1_stored_value, mem_cell_2_stored_value, mem_cell_3_stored_value,
       mem_cell_4_stored_value, mem_cell_5_stored_value, mem_cell_6_stored_value, mem_cell_7_stored_value,
       mem_cell_8_stored_value, mem_cell_9_stored_value, mem_cell_10_stored_value, mem_cell_11_stored_value,
       mem_cell_12_stored_value, mem_cell_13_stored_value, mem_cell_14_stored_value,
       mem_cell_15_stored_value, mem_cell_16_stored_value, mem_cell_17_stored_value,
       mem_cell_18_stored_value, mem_cell_19_stored_value, mem_cell_20_stored_value,
       mem_cell_21_stored_value, mem_cell_22_stored_value, mem_cell_23_stored_value,
       mem_cell_24_stored_value, mem_cell_25_stored_value, mem_cell_26_stored_value,
       mem_cell_27_stored_value, mem_cell_28_stored_value, mem_cell_29_stored_value,
       mem_cell_30_stored_value, mem_cell_31_stored_value, mem_cell_32_stored_value,
       register_8_1_output_value;

  REGISTER_8 register_8_1 (
    .stored_value(stored_address), .output_value(register_8_1_output_value), .input_value(address),
    .set(set), .enable(1'b1));
  DECODER_4x16 decoder_4x16_1 (
    .out_16(decoder_4x16_1_out_16), .finish(decoder_4x16_1_finish), .start(decoder_4x16_1_start),
    .out_3(decoder_4x16_1_out_3), .out_4(decoder_4x16_1_out_4), .out_5(decoder_4x16_1_out_5),
    .out_6(decoder_4x16_1_out_6), .out_7(decoder_4x16_1_out_7), .out_8(decoder_4x16_1_out_8),
    .out_9(decoder_4x16_1_out_9), .out_10(decoder_4x16_1_out_10), .out_11(decoder_4x16_1_out_11),
    .out_12(decoder_4x16_1_out_12), .out_13(decoder_4x16_1_out_13), .out_14(decoder_4x16_1_out_14),
    .out_15(decoder_4x16_1_out_15), .in_1(register_8_1_output_value[7:4]));
  // Probe on mem_cell_1_stored_value
  MEM_CELL mem_cell_1 (
    .output_value(output_val), .stored_value(mem_cell_1_stored_value), .input_value(input_val),
    .reset(reset), .horisontal_address(decoder_4x16_1_start), .vertical_address(decoder_4x16_2_finish),
    .set(set_value), .enable(enable_read));
  // Probe on mem_cell_2_stored_value
  MEM_CELL mem_cell_2 (
    .output_value(output_val), .stored_value(mem_cell_2_stored_value), .input_value(input_val),
    .reset(reset), .horisontal_address(decoder_4x16_1_out_3), .vertical_address(decoder_4x16_2_finish),
    .set(set_value), .enable(enable_read));
  // Probe on mem_cell_3_stored_value
  MEM_CELL mem_cell_3 (
    .output_value(output_val), .stored_value(mem_cell_3_stored_value), .input_value(input_val),
    .reset(reset), .horisontal_address(decoder_4x16_1_start), .vertical_address(decoder_4x16_2_out_16),
    .set(set_value), .enable(enable_read));
  // Probe on mem_cell_4_stored_value
  MEM_CELL mem_cell_4 (
    .output_value(output_val), .stored_value(mem_cell_4_stored_value), .input_value(input_val),
    .reset(reset), .horisontal_address(decoder_4x16_1_out_3), .vertical_address(decoder_4x16_2_out_16),
    .set(set_value), .enable(enable_read));
  // Probe on mem_cell_5_stored_value
  MEM_CELL mem_cell_5 (
    .output_value(output_val), .stored_value(mem_cell_5_stored_value), .input_value(input_val),
    .reset(reset), .horisontal_address(decoder_4x16_1_start), .vertical_address(decoder_4x16_2_out_15),
    .set(set_value), .enable(enable_read));
  // Probe on mem_cell_6_stored_value
  MEM_CELL mem_cell_6 (
    .output_value(output_val), .stored_value(mem_cell_6_stored_value), .input_value(input_val),
    .reset(reset), .horisontal_address(decoder_4x16_1_out_3), .vertical_address(decoder_4x16_2_out_15),
    .set(set_value), .enable(enable_read));
  // Probe on mem_cell_7_stored_value
  MEM_CELL mem_cell_7 (
    .output_value(output_val), .stored_value(mem_cell_7_stored_value), .input_value(input_val),
    .reset(reset), .horisontal_address(decoder_4x16_1_start), .vertical_address(decoder_4x16_2_out_14),
    .set(set_value), .enable(enable_read));
  // Probe on mem_cell_8_stored_value
  MEM_CELL mem_cell_8 (
    .output_value(output_val), .stored_value(mem_cell_8_stored_value), .input_value(input_val),
    .reset(reset), .horisontal_address(decoder_4x16_1_out_3), .vertical_address(decoder_4x16_2_out_14),
    .set(set_value), .enable(enable_read));
  // Probe on mem_cell_9_stored_value
  MEM_CELL mem_cell_9 (
    .output_value(output_val), .stored_value(mem_cell_9_stored_value), .input_value(input_val),
    .reset(reset), .horisontal_address(decoder_4x16_1_start), .vertical_address(decoder_4x16_2_out_13),
    .set(set_value), .enable(enable_read));
  // Probe on mem_cell_10_stored_value
  MEM_CELL mem_cell_10 (
    .output_value(output_val), .stored_value(mem_cell_10_stored_value), .input_value(input_val),
    .reset(reset), .horisontal_address(decoder_4x16_1_out_3), .vertical_address(decoder_4x16_2_out_13),
    .set(set_value), .enable(enable_read));
  // Probe on mem_cell_11_stored_value
  MEM_CELL mem_cell_11 (
    .output_value(output_val), .stored_value(mem_cell_11_stored_value), .input_value(input_val),
    .reset(reset), .horisontal_address(decoder_4x16_1_start), .vertical_address(decoder_4x16_2_out_12),
    .set(set_value), .enable(enable_read));
  // Probe on mem_cell_12_stored_value
  MEM_CELL mem_cell_12 (
    .output_value(output_val), .stored_value(mem_cell_12_stored_value), .input_value(input_val),
    .reset(reset), .horisontal_address(decoder_4x16_1_out_3), .vertical_address(decoder_4x16_2_out_12),
    .set(set_value), .enable(enable_read));
  // Probe on mem_cell_13_stored_value
  MEM_CELL mem_cell_13 (
    .output_value(output_val), .stored_value(mem_cell_13_stored_value), .input_value(input_val),
    .reset(reset), .horisontal_address(decoder_4x16_1_start), .vertical_address(decoder_4x16_2_out_11),
    .set(set_value), .enable(enable_read));
  // Probe on mem_cell_14_stored_value
  MEM_CELL mem_cell_14 (
    .output_value(output_val), .stored_value(mem_cell_14_stored_value), .input_value(input_val),
    .reset(reset), .horisontal_address(decoder_4x16_1_out_3), .vertical_address(decoder_4x16_2_out_11),
    .set(set_value), .enable(enable_read));
  DECODER_4x16 decoder_4x16_2 (
    .out_16(decoder_4x16_2_out_16), .finish(decoder_4x16_2_finish), .start(decoder_4x16_2_start),
    .out_3(decoder_4x16_2_out_3), .out_4(decoder_4x16_2_out_4), .out_5(decoder_4x16_2_out_5),
    .out_6(decoder_4x16_2_out_6), .out_7(decoder_4x16_2_out_7), .out_8(decoder_4x16_2_out_8),
    .out_9(decoder_4x16_2_out_9), .out_10(decoder_4x16_2_out_10), .out_11(decoder_4x16_2_out_11),
    .out_12(decoder_4x16_2_out_12), .out_13(decoder_4x16_2_out_13), .out_14(decoder_4x16_2_out_14),
    .out_15(decoder_4x16_2_out_15), .in_1(register_8_1_output_value[3:0]));
  // Probe on mem_cell_15_stored_value
  MEM_CELL mem_cell_15 (
    .output_value(output_val), .stored_value(mem_cell_15_stored_value), .input_value(input_val),
    .reset(reset), .horisontal_address(decoder_4x16_1_start), .vertical_address(decoder_4x16_2_out_10),
    .set(set_value), .enable(enable_read));
  // Probe on mem_cell_16_stored_value
  MEM_CELL mem_cell_16 (
    .output_value(output_val), .stored_value(mem_cell_16_stored_value), .input_value(input_val),
    .reset(reset), .horisontal_address(decoder_4x16_1_out_3), .vertical_address(decoder_4x16_2_out_10),
    .set(set_value), .enable(enable_read));
  // Probe on mem_cell_17_stored_value
  MEM_CELL mem_cell_17 (
    .output_value(output_val), .stored_value(mem_cell_17_stored_value), .input_value(input_val),
    .reset(reset), .horisontal_address(decoder_4x16_1_start), .vertical_address(decoder_4x16_2_out_9),
    .set(set_value), .enable(enable_read));
  // Probe on mem_cell_18_stored_value
  MEM_CELL mem_cell_18 (
    .output_value(output_val), .stored_value(mem_cell_18_stored_value), .input_value(input_val),
    .reset(reset), .horisontal_address(decoder_4x16_1_out_3), .vertical_address(decoder_4x16_2_out_9),
    .set(set_value), .enable(enable_read));
  // Probe on mem_cell_19_stored_value
  MEM_CELL mem_cell_19 (
    .output_value(output_val), .stored_value(mem_cell_19_stored_value), .input_value(input_val),
    .reset(reset), .horisontal_address(decoder_4x16_1_start), .vertical_address(decoder_4x16_2_out_8),
    .set(set_value), .enable(enable_read));
  // Probe on mem_cell_20_stored_value
  MEM_CELL mem_cell_20 (
    .output_value(output_val), .stored_value(mem_cell_20_stored_value), .input_value(input_val),
    .reset(reset), .horisontal_address(decoder_4x16_1_out_3), .vertical_address(decoder_4x16_2_out_8),
    .set(set_value), .enable(enable_read));
  // Probe on mem_cell_21_stored_value
  MEM_CELL mem_cell_21 (
    .output_value(output_val), .stored_value(mem_cell_21_stored_value), .input_value(input_val),
    .reset(reset), .horisontal_address(decoder_4x16_1_start), .vertical_address(decoder_4x16_2_out_7),
    .set(set_value), .enable(enable_read));
  // Probe on mem_cell_22_stored_value
  MEM_CELL mem_cell_22 (
    .output_value(output_val), .stored_value(mem_cell_22_stored_value), .input_value(input_val),
    .reset(reset), .horisontal_address(decoder_4x16_1_out_3), .vertical_address(decoder_4x16_2_out_7),
    .set(set_value), .enable(enable_read));
  // Probe on mem_cell_23_stored_value
  MEM_CELL mem_cell_23 (
    .output_value(output_val), .stored_value(mem_cell_23_stored_value), .input_value(input_val),
    .reset(reset), .horisontal_address(decoder_4x16_1_start), .vertical_address(decoder_4x16_2_out_6),
    .set(set_value), .enable(enable_read));
  // Probe on mem_cell_24_stored_value
  MEM_CELL mem_cell_24 (
    .output_value(output_val), .stored_value(mem_cell_24_stored_value), .input_value(input_val),
    .reset(reset), .horisontal_address(decoder_4x16_1_out_3), .vertical_address(decoder_4x16_2_out_6),
    .set(set_value), .enable(enable_read));
  // Probe on mem_cell_25_stored_value
  MEM_CELL mem_cell_25 (
    .output_value(output_val), .stored_value(mem_cell_25_stored_value), .input_value(input_val),
    .reset(reset), .horisontal_address(decoder_4x16_1_start), .vertical_address(decoder_4x16_2_out_5),
    .set(set_value), .enable(enable_read));
  // Probe on mem_cell_26_stored_value
  MEM_CELL mem_cell_26 (
    .output_value(output_val), .stored_value(mem_cell_26_stored_value), .input_value(input_val),
    .reset(reset), .horisontal_address(decoder_4x16_1_out_3), .vertical_address(decoder_4x16_2_out_5),
    .set(set_value), .enable(enable_read));
  // Probe on mem_cell_27_stored_value
  MEM_CELL mem_cell_27 (
    .output_value(output_val), .stored_value(mem_cell_27_stored_value), .input_value(input_val),
    .reset(reset), .horisontal_address(decoder_4x16_1_start), .vertical_address(decoder_4x16_2_out_4),
    .set(set_value), .enable(enable_read));
  // Probe on mem_cell_28_stored_value
  MEM_CELL mem_cell_28 (
    .output_value(output_val), .stored_value(mem_cell_28_stored_value), .input_value(input_val),
    .reset(reset), .horisontal_address(decoder_4x16_1_out_3), .vertical_address(decoder_4x16_2_out_4),
    .set(set_value), .enable(enable_read));
  // Probe on mem_cell_29_stored_value
  MEM_CELL mem_cell_29 (
    .output_value(output_val), .stored_value(mem_cell_29_stored_value), .input_value(input_val),
    .reset(reset), .horisontal_address(decoder_4x16_1_start), .vertical_address(decoder_4x16_2_out_3),
    .set(set_value), .enable(enable_read));
  // Probe on mem_cell_30_stored_value
  MEM_CELL mem_cell_30 (
    .output_value(output_val), .stored_value(mem_cell_30_stored_value), .input_value(input_val),
    .reset(reset), .horisontal_address(decoder_4x16_1_out_3), .vertical_address(decoder_4x16_2_out_3),
    .set(set_value), .enable(enable_read));
  // Probe on mem_cell_31_stored_value
  MEM_CELL mem_cell_31 (
    .output_value(output_val), .stored_value(mem_cell_31_stored_value), .input_value(input_val),
    .reset(reset), .horisontal_address(decoder_4x16_1_start), .vertical_address(decoder_4x16_2_start),
    .set(set_value), .enable(enable_read));
  // Probe on mem_cell_32_stored_value
  MEM_CELL mem_cell_32 (
    .output_value(output_val), .stored_value(mem_cell_32_stored_value), .input_value(input_val),
    .reset(reset), .horisontal_address(decoder_4x16_1_out_3), .vertical_address(decoder_4x16_2_start),
    .set(set_value), .enable(enable_read));
endmodule

module HALF_ADDER (
  input  a,
  input  b,
  output s,
  output carry
);

  xor xor_1 (s, a, b);
  and and_1 (carry, a, b);
endmodule

module FULL_ADDER (
  input  carry_in,
  input  a,
  input  b,
  output sum,
  output carry_out
);

  wire half_adder_1_s;

  HALF_ADDER half_adder_1 (.s(half_adder_1_s), .a(a), .b(b));  // open: carry
  HALF_ADDER half_adder_2 (.s(sum), .carry(carry_out), .a(carry_in), .b(half_adder_1_s));
endmodule

module ADDER_8 (
  input  [7:0] a,
  input  [7:0] b,
  input  carry_in,
  output carry_out,
  output [7:0] sum
);

  wire full_adder_2_carry_out, full_adder_3_carry_out, full_adder_4_carry_out, full_adder_5_carry_out,
       full_adder_6_carry_out, full_adder_7_carry_out, full_adder_8_carry_out;

  FULL_ADDER full_adder_1 (.sum(sum[7]), .carry_out(carry_out), .carry_in(full_adder_2_carry_out), .a(a[7]), .b(b[7]));
  FULL_ADDER full_adder_2 (
    .sum(sum[6]), .carry_out(full_adder_2_carry_out), .carry_in(full_adder_3_carry_out), .a(a[6]), .b(b[6]));
  FULL_ADDER full_adder_3 (
    .sum(sum[5]), .carry_out(full_adder_3_carry_out), .carry_in(full_adder_4_carry_out), .a(a[5]), .b(b[5]));
  FULL_ADDER full_adder_4 (
    .sum(sum[4]), .carry_out(full_adder_4_carry_out), .carry_in(full_adder_5_carry_out), .a(a[4]), .b(b[4]));
  FULL_ADDER full_adder_5 (
    .sum(sum[3]), .carry_out(full_adder_5_carry_out), .carry_in(full_adder_6_carry_out), .a(a[3]), .b(b[3]));
  FULL_ADDER full_adder_6 (
    .sum(sum[2]), .carry_out(full_adder_6_carry_out), .carry_in(full_adder_7_carry_out), .a(a[2]), .b(b[2]));
  FULL_ADDER full_adder_7 (
    .sum(sum[1]), .carry_out(full_adder_7_carry_out), .carry_in(full_adder_8_carry_out), .a(a[1]), .b(b[1]));
  FULL_ADDER full_adder_8 (.sum(sum[0]), .carry_out(full_adder_8_carry_out), .carry_in(carry_in), .a(a[0]), .b(b[0]));
endmodule

module SHIFT_LEFT (
  input  [7:0] value_in,
  input  shift_in,
  output shift_out,
  output [7:0] value_out
);

  wire [6:0] mem_8_1_output_value;

  MEM_8 mem_8_1 (.output_value({shift_out, mem_8_1_output_value}), .set(1'b1), .input_value(value_in));
  MEM_8 mem_8_2 (.output_value(value_out), .set(1'b1), .input_value({mem_8_1_output_value, shift_in}));
endmodule

module SHIFT_RIGHT (
  input  shift_in,
  input  [7:0] value_in,
  output [7:0] value_out,
  output shift_out
);

  wire [7:1] mem_8_1_output_value;

  MEM_8 mem_8_1 (.output_value({mem_8_1_output_value, shift_out}), .set(1'b1), .input_value(value_in));
  MEM_8 mem_8_2 (.output_value(value_out), .set(1'b1), .input_value({shift_in, mem_8_1_output_value}));
endmodule

module NOT_8 (
  input  [7:0] in_1,
  output [7:0] out_2
);

  not not_1 (out_2[7], in_1[7]);
  not not_2 (out_2[6], in_1[6]);
  not not_3 (out_2[5], in_1[5]);
  not not_4 (out_2[4], in_1[4]);
  not not_5 (out_2[3], in_1[3]);
  not not_6 (out_2[2], in_1[2]);
  not not_7 (out_2[1], in_1[1]);
  not not_8 (out_2[0], in_1[0]);
endmodule

module AND_2x8 (
  input  [7:0] a,
  input  [7:0] b,
  output [7:0] a_and_b
);

  and and_1 (a_and_b[7], a[7], b[7]);
  and and_2 (a_and_b[6], a[6], b[6]);
  and and_3 (a_and_b[5], a[5], b[5]);
  and and_4 (a_and_b[4], a[4], b[4]);
  and and_5 (a_and_b[3], a[3], b[3]);
  and and_6 (a_and_b[2], a[2], b[2]);
  and and_7 (a_and_b[1], a[1], b[1]);
  and and_8 (a_and_b[0], a[0], b[0]);
endmodule

module OR_2x8 (
  input  [7:0] a,
  input  [7:0] b,
  output [7:0] a_or_b
);

  or or_1 (a_or_b[7], a[7], b[7]);
  or or_2 (a_or_b[6], a[6], b[6]);
  or or_3 (a_or_b[5], a[5], b[5]);
  or or_4 (a_or_b[4], a[4], b[4]);
  or or_5 (a_or_b[3], a[3], b[3]);
  or or_6 (a_or_b[2], a[2], b[2]);
  or or_7 (a_or_b[1], a[1], b[1]);
  or or_8 (a_or_b[0], a[0], b[0]);
endmodule

module XOR_2x8 (
  input  [7:0] a,
  input  [7:0] b,
  output [7:0] a_xor_b
);

  xor xor_1 (a_xor_b[7], a[7], b[7]);
  xor xor_2 (a_xor_b[6], a[6], b[6]);
  xor xor_3 (a_xor_b[5], a[5], b[5]);
  xor xor_4 (a_xor_b[4], a[4], b[4]);
  xor xor_5 (a_xor_b[3], a[3], b[3]);
  xor xor_6 (a_xor_b[2], a[2], b[2]);
  xor xor_7 (a_xor_b[1], a[1], b[1]);
  xor xor_8 (a_xor_b[0], a[0], b[0]);
endmodule

module COMPARATOR_1 (
  input  equal_above,
  input  a_larger_above,
  input  a,
  input  b,
  output a_xor_b,
  output equal,
  output a_larger
);

  wire and_2_out;

  xor xor_1 (a_xor_b, a, b);
  and and_1 (equal, ~a_xor_b, equal_above);  // AND_Gate
  and and_2 (and_2_out, equal_above, a, a_xor_b);
  or or_1 (a_larger, and_2_out, a_larger_above);
endmodule

module COMPARATOR_8 (
  input  [7:0] a,
  input  [7:0] b,
  output [7:0] a_xor_b,
  output a_larger_than_b,
  output equal
);

  wire comparator_1_1_a_larger, comparator_1_1_equal, comparator_1_2_a_larger, comparator_1_2_equal,
       comparator_1_3_a_larger, comparator_1_3_equal, comparator_1_4_a_larger, comparator_1_4_equal,
       comparator_1_5_a_larger, comparator_1_5_equal, comparator_1_6_a_larger, comparator_1_6_equal,
       comparator_1_7_a_larger, comparator_1_7_equal;

  COMPARATOR_1 comparator_1_1 (
    .equal(comparator_1_1_equal), .a_larger(comparator_1_1_a_larger), .a_xor_b(a_xor_b[7]),
    .equal_above(1'b1), .a_larger_above(1'b0), .a(a[7]), .b(b[7]));
  COMPARATOR_1 comparator_1_2 (
    .equal(comparator_1_2_equal), .a_larger(comparator_1_2_a_larger), .a_xor_b(a_xor_b[6]),
    .equal_above(comparator_1_1_equal), .a_larger_above(comparator_1_1_a_larger), .a(a[6]), .b(b[6]));
  COMPARATOR_1 comparator_1_3 (
    .equal(comparator_1_3_equal), .a_larger(comparator_1_3_a_larger), .a_xor_b(a_xor_b[5]),
    .equal_above(comparator_1_2_equal), .a_larger_above(comparator_1_2_a_larger), .a(a[5]), .b(b[5]));
  COMPARATOR_1 comparator_1_4 (
    .equal(comparator_1_4_equal), .a_larger(comparator_1_4_a_larger), .a_xor_b(a_xor_b[4]),
    .equal_above(comparator_1_3_equal), .a_larger_above(comparator_1_3_a_larger), .a(a[4]), .b(b[4]));
  COMPARATOR_1 comparator_1_5 (
    .equal(comparator_1_5_equal), .a_larger(comparator_1_5_a_larger), .a_xor_b(a_xor_b[3]),
    .equal_above(comparator_1_4_equal), .a_larger_above(comparator_1_4_a_larger), .a(a[3]), .b(b[3]));
  COMPARATOR_1 comparator_1_6 (
    .equal(comparator_1_6_equal), .a_larger(comparator_1_6_a_larger), .a_xor_b(a_xor_b[2]),
    .equal_above(comparator_1_5_equal), .a_larger_above(comparator_1_5_a_larger), .a(a[2]), .b(b[2]));
  COMPARATOR_1 comparator_1_7 (
    .equal(comparator_1_7_equal), .a_larger(comparator_1_7_a_larger), .a_xor_b(a_xor_b[1]),
    .equal_above(comparator_1_6_equal), .a_larger_above(comparator_1_6_a_larger), .a(a[1]), .b(b[1]));
  COMPARATOR_1 comparator_1_8 (
    .equal(equal), .a_larger(a_larger_than_b), .a_xor_b(a_xor_b[0]), .equal_above(comparator_1_7_equal),
    .a_larger_above(comparator_1_7_a_larger), .a(a[0]), .b(b[0]));
endmodule

module Z (
  input  [7:0] in_1,
  output zero_out
);

  wire or_1_out;

  or or_1 (or_1_out, in_1[0], in_1[1], in_1[2], in_1[3], in_1[4], in_1[5], in_1[6], in_1[7]);
  not not_1 (zero_out, or_1_out);
endmodule

module ALU (
  input  [7:0] a,
  input  [7:0] b,
  input  carry_in,
  input  [2:0] operation,
  output a_larger_than_b,
  output equal,
  output zero,
  output [7:0] result,
  output carry_out
);

  wire adder_8_1_carry_out, decoder_3x8_1_out_3, decoder_3x8_1_out_4, decoder_3x8_1_out_5,
       decoder_3x8_1_out_6, decoder_3x8_1_out_7, decoder_3x8_1_out_8, decoder_3x8_1_start,
       shift_left_1_shift_out, shift_right_1_shift_out;
  wire [7:0] adder_8_1_sum, and_2x8_1_a_and_b, comparator_8_1_a_xor_b, not_8_1_out_2, or_2x8_1_a_or_b,
       shift_left_1_value_out, shift_right_1_value_out;

  COMPARATOR_8 comparator_8_1 (
    .a_xor_b(comparator_8_1_a_xor_b), .a_larger_than_b(a_larger_than_b), .equal(equal), .a(a), .b(b));
  OR_2x8 or_2x8_1 (.a_or_b(or_2x8_1_a_or_b), .a(a), .b(b));
  AND_2x8 and_2x8_1 (.a_and_b(and_2x8_1_a_and_b), .a(a), .b(b));
  NOT_8 not_8_1 (.out_2(not_8_1_out_2), .in_1(a));
  SHIFT_LEFT shift_left_1 (
    .shift_out(shift_left_1_shift_out), .value_out(shift_left_1_value_out), .shift_in(carry_in), .value_in(a));
  SHIFT_RIGHT shift_right_1 (
    .value_out(shift_right_1_value_out), .shift_out(shift_right_1_shift_out), .value_in(a),
    .shift_in(carry_in));
  assign carry_out = decoder_3x8_1_start ? adder_8_1_carry_out : 1'bz;  // Controlled_Buffer controlled_buffer_1
  ADDER_8 adder_8_1 (.carry_out(adder_8_1_carry_out), .sum(adder_8_1_sum), .a(a), .b(b), .carry_in(carry_in));
  assign result = decoder_3x8_1_out_5 ? not_8_1_out_2 : 8'bz;  // Controlled_Buffer controlled_buffer_2
  assign carry_out = decoder_3x8_1_out_4 ? shift_left_1_shift_out : 1'bz;  // Controlled_Buffer controlled_buffer_3
  assign result = decoder_3x8_1_out_4 ? shift_left_1_value_out : 8'bz;  // Controlled_Buffer controlled_buffer_4
  assign result = decoder_3x8_1_out_3 ? shift_right_1_value_out : 8'bz;  // Controlled_Buffer controlled_buffer_5
  assign carry_out = decoder_3x8_1_out_3 ? shift_right_1_shift_out : 1'bz;  // Controlled_Buffer controlled_buffer_6
  assign result = decoder_3x8_1_start ? adder_8_1_sum : 8'bz;  // Controlled_Buffer controlled_buffer_7
  DECODER_3x8 decoder_3x8_1 (
    .start(decoder_3x8_1_start), .out_3(decoder_3x8_1_out_3), .out_4(decoder_3x8_1_out_4),
    .out_5(decoder_3x8_1_out_5), .out_6(decoder_3x8_1_out_6), .out_7(decoder_3x8_1_out_7),
    .out_8(decoder_3x8_1_out_8), .in_1(operation));  // open: finish
  assign result = decoder_3x8_1_out_8 ? comparator_8_1_a_xor_b : 8'bz;  // Controlled_Buffer controlled_buffer_8
  assign result = decoder_3x8_1_out_7 ? or_2x8_1_a_or_b : 8'bz;  // Controlled_Buffer controlled_buffer_9
  assign result = decoder_3x8_1_out_6 ? and_2x8_1_a_and_b : 8'bz;  // Controlled_Buffer controlled_buffer_10
  Z z_1 (.zero_out(zero), .in_1(result));

  // Notes on the sheet:
  //   The Arithmetic and Logic Unit
  //   Instruction Set
  //   000    ADD
  //   001    SHR
  //   010    SHL
  //   011    NOT
  //   100    AND
  //   101    OR
  //   110    XOR
  //   111    CMP - compare
endmodule

module CLK (
  input  clk_in,
  output clk_s,
  output clk_out,
  output clk_e
);

  wire j_k_ff_1_qn;

  J_K_Flip_Flop j_k_ff_1 (.J(1'b1), .K(1'b1), .clk(clk_in), .Q(clk_out), .Qn(j_k_ff_1_qn));  // open: preset, reset
  and and_1 (clk_s, clk_in, clk_out);
  nand nand_1 (clk_e, j_k_ff_1_qn, clk_in);
endmodule

module BUS_1 (
  input  [7:0] input_value,
  input  bus_one,
  output [7:0] output_value
);

  wire not_1_out;

  and and_1 (output_value[6], input_value[6], not_1_out);
  and and_2 (output_value[7], input_value[7], not_1_out);
  and and_3 (output_value[5], input_value[5], not_1_out);
  and and_4 (output_value[4], input_value[4], not_1_out);
  and and_5 (output_value[3], input_value[3], not_1_out);
  and and_6 (output_value[2], input_value[2], not_1_out);
  and and_7 (output_value[1], input_value[1], not_1_out);
  not not_1 (not_1_out, bus_one);
  or or_1 (output_value[0], input_value[0], bus_one);
endmodule

module STEPPER (
  input  clock,
  output out_2,
  output out_3,
  output out_4,
  output out_5,
  output out_6,
  output out_7
);

  wire d_ff_1_q, d_ff_2_q, d_ff_3_q, d_ff_4_q, d_ff_5_q, d_ff_6_q;

  D_Flip_Flop #(.trigger("falling")) d_ff_1 (
    .D(1'b1), .clk(clock), .Q(d_ff_1_q), .reset(d_ff_6_q));  // open: Qn, preset
  and and_1 (out_2, 1'b1, ~d_ff_1_q);  // AND_Gate
  D_Flip_Flop #(.trigger("falling")) d_ff_2 (
    .D(d_ff_1_q), .clk(clock), .Q(d_ff_2_q), .reset(d_ff_6_q));  // open: Qn, preset
  and and_2 (out_3, d_ff_1_q, ~d_ff_2_q);  // AND_Gate
  D_Flip_Flop #(.trigger("falling")) d_ff_3 (
    .D(d_ff_2_q), .clk(clock), .Q(d_ff_3_q), .reset(d_ff_6_q));  // open: Qn, preset
  and and_3 (out_4, d_ff_2_q, ~d_ff_3_q);  // AND_Gate
  D_Flip_Flop #(.trigger("falling")) d_ff_4 (
    .D(d_ff_3_q), .clk(clock), .Q(d_ff_4_q), .reset(d_ff_6_q));  // open: Qn, preset
  and and_4 (out_5, d_ff_3_q, ~d_ff_4_q);  // AND_Gate
  D_Flip_Flop #(.trigger("falling")) d_ff_5 (
    .D(d_ff_4_q), .clk(clock), .Q(d_ff_5_q), .reset(d_ff_6_q));  // open: Qn, preset
  and and_5 (out_6, d_ff_4_q, ~d_ff_5_q);  // AND_Gate
  D_Flip_Flop #(.trigger("falling")) d_ff_6 (
    .D(d_ff_5_q), .clk(clock), .Q(d_ff_6_q), .reset(d_ff_6_q));  // open: Qn, preset
  and and_6 (out_7, d_ff_5_q, ~d_ff_6_q);  // AND_Gate
endmodule

module clk_demo (
  input  in_1
);

  wire clk_1_clk_e, clk_1_clk_out, clk_1_clk_s, digital_oscilloscope_1_p1;

  CLK clk_1 (.clk_out(clk_1_clk_out), .clk_e(clk_1_clk_e), .clk_s(clk_1_clk_s), .clk_in(digital_oscilloscope_1_p1));
  // Digital_Oscilloscope digital_oscilloscope_1: pin names not known; wires that end beside it: digital_oscilloscope_1_p1, clk_1_clk_out, clk_1_clk_s, clk_1_clk_e, in_1
  Clock clock_1 (.out(digital_oscilloscope_1_p1));
endmodule

module cpu_demo_0 (
  input  in_1,
  input  in_2,
  input  in_3,
  input  in_4,
  input  in_5,
  input  in_6,
  input  in_7,
  input  in_8,
  input  in_9,
  input  in_10,
  input  [2:0] in_11,
  input  in_12,
  input  in_13,
  input  in_14,
  input  in_15,
  input  in_16,
  input  in_17,
  input  in_18,
  input  [7:0] in_19,
  input  in_20
);

  wire alu_1_a_larger_than_b, alu_1_carry_out, alu_1_equal, alu_1_zero, clock_1_out;
  wire [7:0] alu_1_result, bus_1_1_output_value, ram_256_1_stored_address, reg_accumulator_1_output_value,
       reg_accumulator_1_stored_value, reg_tmp_1_output_value, register_8_1_stored_value,
       register_8_2_stored_value, register_8_3_stored_value, register_8_4_stored_value;

  REG_TMP reg_tmp_1 (.output_value(reg_tmp_1_output_value), .set(in_1), .input_value(reg_accumulator_1_output_value));
  // Probe on reg_tmp_1_output_value
  BUS_1 bus_1_1 (.output_value(bus_1_1_output_value), .input_value(reg_tmp_1_output_value), .bus_one(in_10));
  // Probe on alu_1_result
  ALU alu_1 (
    .zero(alu_1_zero), .result(alu_1_result), .a_larger_than_b(alu_1_a_larger_than_b),
    .carry_out(alu_1_carry_out), .equal(alu_1_equal), .a(reg_accumulator_1_output_value),
    .b(bus_1_1_output_value), .carry_in(in_12), .operation(in_11));
  // Probe on alu_1_carry_out
  // Probe on alu_1_a_larger_than_b
  // Probe on alu_1_equal
  // Probe on alu_1_zero
  REG_ACCUMULATOR reg_accumulator_1 (
    .stored_value(reg_accumulator_1_stored_value), .output_value(reg_accumulator_1_output_value),
    .set(in_16), .enable(in_17), .input_value(alu_1_result));
  // Probe on reg_accumulator_1_stored_value
  // Probe on register_8_1_stored_value
  REGISTER_8 register_8_1 (
    .stored_value(register_8_1_stored_value), .output_value(reg_accumulator_1_output_value),
    .input_value(reg_accumulator_1_output_value), .set(in_2), .enable(in_3));
  assign reg_accumulator_1_output_value = in_20 ? in_19 : 8'bz;  // Controlled_Buffer controlled_buffer_1
  // Probe on register_8_2_stored_value
  REGISTER_8 register_8_2 (
    .stored_value(register_8_2_stored_value), .output_value(reg_accumulator_1_output_value),
    .input_value(reg_accumulator_1_output_value), .set(in_4), .enable(in_5));
  Clock clock_1 (.out(clock_1_out));
  CLK clk_1 (.clk_in(clock_1_out));  // open: clk_out, clk_e, clk_s
  // Probe on register_8_3_stored_value
  REGISTER_8 register_8_3 (
    .stored_value(register_8_3_stored_value), .output_value(reg_accumulator_1_output_value),
    .input_value(reg_accumulator_1_output_value), .set(in_6), .enable(in_7));
  // Probe on reg_accumulator_1_output_value
  // Probe on ram_256_1_stored_address
  // Probe on register_8_4_stored_value
  REGISTER_8 register_8_4 (
    .stored_value(register_8_4_stored_value), .output_value(reg_accumulator_1_output_value),
    .input_value(reg_accumulator_1_output_value), .set(in_8), .enable(in_9));
  RAM_256 ram_256_1 (
    .stored_address(ram_256_1_stored_address), .output_val(reg_accumulator_1_output_value), .set(in_13),
    .enable_read(in_15), .reset(in_18), .set_value(in_14), .address(reg_accumulator_1_output_value),
    .input_val(reg_accumulator_1_output_value));

  // Notes on the sheet:
  //   Instruction Set
  //   000    ADD
  //   001    SHR
  //   010    SHL
  //   011    NOT
  //   100    AND
  //   101    OR
  //   110    XOR
  //   111    CMP - compare
  //   NOTE: ONLY first 16 bytes available in RAM
endmodule

module cpu_demo_1 (
  input  in_1,
  input  in_2,
  input  in_3,
  input  in_4,
  input  in_5,
  input  in_6,
  input  in_7,
  input  in_8,
  input  in_9,
  input  in_10,
  input  [2:0] in_11,
  input  in_12,
  input  in_13,
  input  in_14,
  input  in_15,
  input  in_16,
  input  in_17,
  input  in_18,
  input  [7:0] in_19,
  input  in_20
);

  wire alu_1_a_larger_than_b, alu_1_carry_out, alu_1_equal, alu_1_zero, clock_1_out;
  wire [7:0] alu_1_result, bus_1_1_output_value, ram_256_1_stored_address, reg_accumulator_1_output_value,
       reg_accumulator_1_stored_value, reg_tmp_1_output_value, register_8_1_stored_value,
       register_8_2_stored_value, register_8_3_stored_value, register_8_4_stored_value;

  // Probe on reg_tmp_1_output_value
  REG_TMP reg_tmp_1 (.output_value(reg_tmp_1_output_value), .set(in_1), .input_value(reg_accumulator_1_output_value));
  BUS_1 bus_1_1 (.output_value(bus_1_1_output_value), .input_value(reg_tmp_1_output_value), .bus_one(in_10));
  // Probe on alu_1_result
  ALU alu_1 (
    .zero(alu_1_zero), .result(alu_1_result), .a_larger_than_b(alu_1_a_larger_than_b),
    .carry_out(alu_1_carry_out), .equal(alu_1_equal), .a(reg_accumulator_1_output_value),
    .b(bus_1_1_output_value), .carry_in(in_12), .operation(in_11));
  // Probe on alu_1_carry_out
  // Probe on alu_1_a_larger_than_b
  // Probe on alu_1_equal
  // Probe on alu_1_zero
  REG_ACCUMULATOR reg_accumulator_1 (
    .stored_value(reg_accumulator_1_stored_value), .output_value(reg_accumulator_1_output_value),
    .set(in_16), .enable(in_17), .input_value(alu_1_result));
  // Probe on reg_accumulator_1_stored_value
  REGISTER_8 register_8_1 (
    .stored_value(register_8_1_stored_value), .output_value(reg_accumulator_1_output_value),
    .input_value(reg_accumulator_1_output_value), .set(in_2), .enable(in_3));
  // Probe on register_8_1_stored_value
  assign reg_accumulator_1_output_value = in_20 ? in_19 : 8'bz;  // Controlled_Buffer controlled_buffer_1
  // Probe on register_8_2_stored_value
  REGISTER_8 register_8_2 (
    .stored_value(register_8_2_stored_value), .output_value(reg_accumulator_1_output_value),
    .input_value(reg_accumulator_1_output_value), .set(in_4), .enable(in_5));
  // Probe on reg_accumulator_1_output_value
  // Probe on register_8_3_stored_value
  REGISTER_8 register_8_3 (
    .stored_value(register_8_3_stored_value), .output_value(reg_accumulator_1_output_value),
    .input_value(reg_accumulator_1_output_value), .set(in_6), .enable(in_7));
  Clock clock_1 (.out(clock_1_out));
  CLK clk_1 (.clk_in(clock_1_out));  // open: clk_out, clk_e, clk_s
  // Probe on register_8_4_stored_value
  REGISTER_8 register_8_4 (
    .stored_value(register_8_4_stored_value), .output_value(reg_accumulator_1_output_value),
    .input_value(reg_accumulator_1_output_value), .set(in_8), .enable(in_9));
  // Probe on ram_256_1_stored_address
  RAM_256 ram_256_1 (
    .stored_address(ram_256_1_stored_address), .output_val(reg_accumulator_1_output_value), .set(in_13),
    .enable_read(in_15), .reset(in_18), .set_value(in_14), .address(reg_accumulator_1_output_value),
    .input_val(reg_accumulator_1_output_value));

  // Notes on the sheet:
  //   Instruction Set
  //   000    ADD
  //   001    SHR
  //   010    SHL
  //   011    NOT
  //   100    AND
  //   101    OR
  //   110    XOR
  //   111    CMP - compare
  //   NOTE: ONLY first 16 bytes available in RAM
endmodule

module control_section_add (
  input  in_1
);

  wire clk_1_clk_e, clk_1_clk_out, clk_1_clk_s, clock_1_out;

  STEPPER stepper_1 (.clock(clk_1_clk_out));  // open: out_2, out_3, out_4, out_5, out_6, out_7
  CLK clk_1 (.clk_out(clk_1_clk_out), .clk_e(clk_1_clk_e), .clk_s(clk_1_clk_s), .clk_in(clock_1_out));
  Clock clock_1 (.out(clock_1_out));
endmodule

module shift_register (
  input  in_1
);

  wire clock_1_out, clock_2_out, d_ff_1_q, d_ff_2_q, j_k_ff_1_q, j_k_ff_2_q;

  Clock clock_1 (.out(clock_1_out));
  D_Flip_Flop d_ff_1 (.D(in_1), .clk(clock_1_out), .Q(d_ff_1_q));  // open: Qn, preset, reset
  J_K_Flip_Flop #(.trigger("falling")) j_k_ff_1 (
    .J(1'b1), .K(1'b1), .clk(clock_2_out), .Q(j_k_ff_1_q));  // open: Qn, preset, reset
  Clock clock_2 (.out(clock_2_out));
  D_Flip_Flop d_ff_2 (.D(d_ff_1_q), .clk(clock_1_out), .Q(d_ff_2_q));  // open: Qn, preset, reset
  J_K_Flip_Flop #(.trigger("falling")) j_k_ff_2 (
    .J(1'b1), .K(1'b1), .clk(j_k_ff_1_q), .Q(j_k_ff_2_q));  // open: Qn, preset, reset
  D_Flip_Flop d_ff_3 (.D(d_ff_2_q), .clk(clock_1_out));  // open: Q, Qn, preset, reset
  J_K_Flip_Flop #(.trigger("falling")) j_k_ff_3 (.J(1'b1), .K(1'b1), .clk(j_k_ff_2_q));  // open: Q, Qn, preset, reset
endmodule

module cpu_alt (
  input  in_1,
  input  in_2,
  input  in_3,
  input  in_4,
  input  in_5,
  input  in_6,
  input  in_7,
  input  in_8,
  input  in_9,
  input  in_10,
  input  [2:0] in_11,
  input  in_12,
  input  in_13,
  input  in_14,
  input  in_15,
  input  in_16,
  input  in_17,
  input  in_18,
  input  [7:0] in_19,
  input  in_20
);

  wire alu_1_a_larger_than_b, alu_1_carry_out, alu_1_equal, alu_1_zero, clock_1_out;
  wire [7:0] alu_1_result, bus_1_1_output_value, ram_256_1_stored_address, reg_accumulator_1_output_value,
       reg_accumulator_1_stored_value, reg_tmp_1_output_value, register_1_q, register_8_1_stored_value,
       register_8_2_stored_value, register_8_3_stored_value;

  // Probe on reg_tmp_1_output_value
  REG_TMP reg_tmp_1 (.output_value(reg_tmp_1_output_value), .set(in_1), .input_value(reg_accumulator_1_output_value));
  BUS_1 bus_1_1 (.output_value(bus_1_1_output_value), .input_value(reg_tmp_1_output_value), .bus_one(in_10));
  // Probe on alu_1_result
  ALU alu_1 (
    .zero(alu_1_zero), .result(alu_1_result), .a_larger_than_b(alu_1_a_larger_than_b),
    .carry_out(alu_1_carry_out), .equal(alu_1_equal), .a(reg_accumulator_1_output_value),
    .b(bus_1_1_output_value), .carry_in(in_12), .operation(in_11));
  // Probe on alu_1_carry_out
  // Probe on alu_1_a_larger_than_b
  // Probe on alu_1_equal
  // Probe on alu_1_zero
  REG_ACCUMULATOR reg_accumulator_1 (
    .stored_value(reg_accumulator_1_stored_value), .output_value(reg_accumulator_1_output_value),
    .set(in_16), .enable(in_17), .input_value(alu_1_result));
  // Probe on reg_accumulator_1_stored_value
  Register register_1 (.D(reg_accumulator_1_output_value), .en(1'b1), .clk(in_2), .Q(register_1_q));  // open: clr
  assign reg_accumulator_1_output_value = in_3 ? register_1_q : 8'bz;  // Controlled_Buffer controlled_buffer_1
  assign reg_accumulator_1_output_value = in_20 ? in_19 : 8'bz;  // Controlled_Buffer controlled_buffer_2
  // Probe on register_8_1_stored_value
  REGISTER_8 register_8_1 (
    .stored_value(register_8_1_stored_value), .output_value(reg_accumulator_1_output_value),
    .input_value(reg_accumulator_1_output_value), .set(in_4), .enable(in_5));
  // Probe on reg_accumulator_1_output_value
  // Probe on register_8_2_stored_value
  REGISTER_8 register_8_2 (
    .stored_value(register_8_2_stored_value), .output_value(reg_accumulator_1_output_value),
    .input_value(reg_accumulator_1_output_value), .set(in_6), .enable(in_7));
  Clock clock_1 (.out(clock_1_out));
  CLK clk_1 (.clk_in(clock_1_out));  // open: clk_out, clk_e, clk_s
  // Probe on register_8_3_stored_value
  REGISTER_8 register_8_3 (
    .stored_value(register_8_3_stored_value), .output_value(reg_accumulator_1_output_value),
    .input_value(reg_accumulator_1_output_value), .set(in_8), .enable(in_9));
  // Probe on ram_256_1_stored_address
  RAM_256 ram_256_1 (
    .stored_address(ram_256_1_stored_address), .output_val(reg_accumulator_1_output_value), .set(in_13),
    .enable_read(in_15), .reset(in_18), .set_value(in_14), .address(reg_accumulator_1_output_value),
    .input_val(reg_accumulator_1_output_value));

  // Notes on the sheet:
  //   Instruction Set
  //   000    ADD
  //   001    SHR
  //   010    SHL
  //   011    NOT
  //   100    AND
  //   101    OR
  //   110    XOR
  //   111    CMP - compare
  //   NOTE: ONLY first 16 bytes available in RAM
endmodule
