// Logisim project ben_eater_CPU.circ as structural Verilog
module ben_eater_cpu_no_control_unit (
  input  in_1,
  input  in_2,
  input  in_3,
  input  in_4,
  input  in_5,
  input  in_6,
  input  in_7,
  input  in_8,
  input  in_9,
  input  in_10,
  input  in_11,
  input  in_12,
  input  in_13,
  input  in_14,
  input  in_15,
  input  in_16
);

  wire ALU_value_carry, clk, decoder_1_out0, decoder_1_out1;
  wire [7:0] adder_1_out, ALU_value, AR_value, BR_value, DR_value, IR_value, main_bus, MAR_value, PC_value,
       RAM_value, subtractor_1_out;

  Register A_register (.D(main_bus), .en(in_1), .clk(clk), .Q(AR_value), .clr(in_12));
  Register B_register (.D(main_bus), .en(in_2), .clk(clk), .Q(BR_value), .clr(in_12));
  Register Display_register (.D(main_bus), .en(in_4), .clk(clk), .Q(DR_value), .clr(in_12));
  // Probe on RAM_value
  // Probe on IR_value
  // Probe on RAM_value
  // Probe on {4'b0000, IR_value[3:0]}
  // Probe on IR_value[7:4]
  Register Instruction_Register (.D(main_bus), .en(in_3), .clk(clk), .Q(IR_value), .clr(in_12));
  // Probe on main_bus
  // Probe on MAR_value
  assign main_bus = in_14 ? RAM_value : 8'bz;  // Controlled_Buffer controlled_buffer_1
  assign main_bus = in_8 ? {4'b0000, IR_value[3:0]} : 8'bz;  // Controlled_Buffer controlled_buffer_2
  Clock clock_1 (.out(clk));
  // Probe on main_bus
  assign main_bus = in_13 ? PC_value : 8'bz;  // Controlled_Buffer controlled_buffer_3
  assign main_bus = in_6 ? AR_value : 8'bz;  // Controlled_Buffer controlled_buffer_4
  assign main_bus = in_15 ? ALU_value : 8'bz;  // Controlled_Buffer controlled_buffer_5
  assign main_bus = in_7 ? BR_value : 8'bz;  // Controlled_Buffer controlled_buffer_6
  Register Memory_address_register (.D(main_bus), .en(in_5), .clk(clk), .Q(MAR_value), .clr(in_12));
  assign ALU_value = decoder_1_out0 ? adder_1_out : 8'bz;  // Controlled_Buffer controlled_buffer_7
  Adder adder_1 (.a(AR_value), .b(BR_value), .out(adder_1_out), .cout(ALU_value_carry));  // open: cin
  assign ALU_value = decoder_1_out1 ? subtractor_1_out : 8'bz;  // Controlled_Buffer controlled_buffer_8
  Subtractor subtractor_1 (.a(AR_value), .b(BR_value), .out(subtractor_1_out));  // open: bin, bout
  Decoder #(.enable("false")) decoder_1 (.out0(decoder_1_out0), .out1(decoder_1_out1), .sel(in_11));
  // Probe on PC_value
  // Probe on AR_value
  // Probe on ALU_value
  // Probe on BR_value
  // Probe on DR_value
  RAM #(.enables("line")) Memory (.addr(MAR_value), .we(in_10), .clk(clk), .din(main_bus), .dout(RAM_value));
  Counter Program_Counter (
    .clr(in_12), .load(in_9), .count(in_16), .clk(clk), .D(main_bus), .Q(PC_value));  // open: up, carry

  // Other names for the same wires on the sheet: ALU_instruction = in_11; ALU_out = in_15; AR_in = in_1;
  //   AR_out = in_6; BR_in = in_2; BR_out = in_7; DR_in = in_4; IR_in = in_3; IR_out = in_8; MAR_in = in_5;
  //   opcode[3:0] = IR_value[7:4]; PC_en = in_16; PC_in = in_9; PC_out = in_13; RAM_in = in_10; RAM_out = in_14;
  //   reset = in_12

  // Notes on the sheet:
  //   ALU
  //   Clock
  //   Instruction Set:
  //   [4 bit opcode] [4 bit operand]
  //   LDA [0001] [memory address] - loads value at memory address to register A
  //   LDB [0010] [memory address] - loads value at memory address to register B
  //   ADD [0011] [memory address] - add AR and BR and stores result to memory address
  //   SUB [0100] [memory address] - subtract BR from AR and stores result to memory address
  //   OUT [0101] [memory address] - loads value at memory address to Display register to display
  //   HALT [1111]                             - halts computer by disabling clock
  //   Program Example:
  //   0x00: 0x1D   // LDA 0x0D
  //   0x01: 0x2E   // LDB 0x0E
  //   0x02: 0x3F   // ADD 0x0F
  //   0x03: 0x5F   // OUT 0x0F
  //   0x04: 0xF0   // HALT
  //   0x0D: 0x20   // 32
  //   0x0E: 0x0A   // 10
  //   Control Unit
  //   0/1 = add/subtract
endmodule

module ben_eater_cpu (
  input  in_1
);

  wire ALU_instruction, ALU_out, ALU_value_carry, AR_in, AR_out, BR_in, BR_out, clk, decoder_1_out0,
       decoder_1_out1, DR_in, IR_in, IR_out, MAR_in, PC_en, PC_in, PC_out, RAM_in, RAM_out, stepper_reset;
  wire [2:0] counter_1_q;
  wire [3:0] register_1_q;
  wire [7:0] adder_1_out, ALU_value, AR_value, BR_value, DR_value, IR_value, main_bus, MAR_value, PC_value,
       RAM_value, subtractor_1_out;

  Register A_register (.D(main_bus), .en(AR_in), .clk(clk), .Q(AR_value), .clr(in_1));
  Register B_register (.D(main_bus), .en(BR_in), .clk(clk), .Q(BR_value), .clr(in_1));
  Register Display_register (.D(main_bus), .en(DR_in), .clk(clk), .Q(DR_value), .clr(in_1));
  // Probe on RAM_value
  // Probe on IR_value
  // Probe on RAM_value
  // Probe on {4'b0000, IR_value[3:0]}
  // Probe on IR_value[7:4]
  Register Instruction_Register (.D(main_bus), .en(IR_in), .clk(clk), .Q(IR_value), .clr(in_1));
  // Probe on main_bus
  // Probe on MAR_value
  assign main_bus = RAM_out ? RAM_value : 8'bz;  // Controlled_Buffer controlled_buffer_1
  assign main_bus = IR_out ? {4'b0000, IR_value[3:0]} : 8'bz;  // Controlled_Buffer controlled_buffer_2
  Clock clock_1 (.out(clk));
  // Probe on main_bus
  assign main_bus = PC_out ? PC_value : 8'bz;  // Controlled_Buffer controlled_buffer_3
  assign main_bus = AR_out ? AR_value : 8'bz;  // Controlled_Buffer controlled_buffer_4
  assign main_bus = ALU_out ? ALU_value : 8'bz;  // Controlled_Buffer controlled_buffer_5
  assign main_bus = BR_out ? BR_value : 8'bz;  // Controlled_Buffer controlled_buffer_6
  Register Memory_address_register (.D(main_bus), .en(MAR_in), .clk(clk), .Q(MAR_value), .clr(in_1));
  assign ALU_value = decoder_1_out0 ? adder_1_out : 8'bz;  // Controlled_Buffer controlled_buffer_7
  Adder adder_1 (.a(AR_value), .b(BR_value), .out(adder_1_out), .cout(ALU_value_carry));  // open: cin
  assign ALU_value = decoder_1_out1 ? subtractor_1_out : 8'bz;  // Controlled_Buffer controlled_buffer_8
  Subtractor subtractor_1 (.a(AR_value), .b(BR_value), .out(subtractor_1_out));  // open: bin, bout
  Decoder #(.enable("false")) decoder_1 (.out0(decoder_1_out0), .out1(decoder_1_out1), .sel(ALU_instruction));
  // Probe on PC_value
  // Probe on AR_value
  // Probe on ALU_value
  // Probe on BR_value
  // Probe on DR_value
  Register #(.trigger("falling"), .width(4)) register_1 (
    .D(IR_value[7:4]), .en(1'b1), .clk(clk), .Q(register_1_q), .clr(in_1));
  RAM #(.enables("line")) Memory (.addr(MAR_value), .we(RAM_in), .clk(clk), .din(main_bus), .dout(RAM_value));
  ROM #(.addrWidth(7), .dataWidth(16)) rom_1 (
    .addr({register_1_q, counter_1_q}),
    .data({stepper_reset, DR_in, ALU_out, ALU_instruction, BR_out, BR_in, AR_out, AR_in, IR_out, IR_in, RAM_out, RAM_in, MAR_in, PC_en, PC_out, PC_in}));
  Counter #(.max('h7), .trigger("falling"), .width(3)) counter_1 (
    .load(stepper_reset), .D(3'b000), .Q(counter_1_q), .clk(clk), .clr(in_1));  // open: count, carry, up
  Counter Program_Counter (
    .load(PC_in), .D(main_bus), .count(PC_en), .Q(PC_value), .clk(clk), .clr(in_1));  // open: carry, up

  // Other names for the same wires on the sheet: opcode[3:0] = IR_value[7:4]; reset = in_1

  // Notes on the sheet:
  //   0/1 = add/subtract
  //   ALU
  //   Clock
  //   Instruction Set:
  //   LDA [0001] [memory address] - loads value at memory address to register A
  //   LDB [0010] [memory address] - loads value at memory address to register B
  //   ADD [0011] [memory address] - add AR and BR and stores result to memory address
  //   SUB [0100] [memory address] - subtract BR from AR and stores result to memory address
  //   OUT [0101] [memory address] - loads value at memory address to Display register to display
  //   HALT [1111]                             - halts computer by disabling clock
  //   contents of rom_1 (hex, n*v repeats v):
  //   8060 7*0 88 124 a 8060 4*0 88 424 a 8060 4*0 88 2014 a 8060 4*0 88 3014 a 8060 4*0 88 4024 a 8060
  //   Control Unit
  //   1
  //   2
  //   4
  //   8
  //   1
  //   2
  //   4
  //   8
  //   1
  //   2
  //   4
  //   8
  //   1
  //   2
  //   4
  //   8
endmodule

module ben_eater_cpu_modified_CU (
  input  in_1,
  output out_2
);

  wire ALU_instruction, ALU_out, ALU_value_carry, AR_in, AR_out, BR_in, BR_out, clk, decoder_1_out0,
       decoder_1_out1, DR_in, IR_in, IR_out, MAR_in, PC_in, RAM_in, RAM_out, stepper_reset;
  wire [2:0] counter_2_q;
  wire [3:0] register_1_q;
  wire [7:0] adder_1_out, ALU_value, AR_value, BR_value, DR_value, IR_value, main_bus, MAR_value, PC_value,
       RAM_value, subtractor_1_out;

  Register A_register (.D(main_bus), .en(AR_in), .clk(clk), .Q(AR_value), .clr(in_1));
  Register B_register (.D(main_bus), .en(BR_in), .clk(clk), .Q(BR_value), .clr(in_1));
  Register Display_register (.D(main_bus), .en(DR_in), .clk(clk), .Q(DR_value), .clr(in_1));
  // Probe on RAM_value
  // Probe on IR_value
  // Probe on RAM_value
  // Probe on {4'b0000, IR_value[3:0]}
  // Probe on IR_value[7:4]
  Register Instruction_Register (.D(main_bus), .en(IR_in), .clk(clk), .Q(IR_value), .clr(in_1));
  // Probe on main_bus
  // Probe on MAR_value
  assign main_bus = RAM_out ? RAM_value : 8'bz;  // Controlled_Buffer controlled_buffer_1
  assign main_bus = IR_out ? {4'b0000, IR_value[3:0]} : 8'bz;  // Controlled_Buffer controlled_buffer_2
  Clock clock_1 (.out(clk));
  // Probe on main_bus
  assign main_bus = MAR_in ? PC_value : 8'bz;  // Controlled_Buffer controlled_buffer_3
  assign main_bus = AR_out ? AR_value : 8'bz;  // Controlled_Buffer controlled_buffer_4
  assign main_bus = ALU_out ? ALU_value : 8'bz;  // Controlled_Buffer controlled_buffer_5
  assign main_bus = BR_out ? BR_value : 8'bz;  // Controlled_Buffer controlled_buffer_6
  Register Memory_address_register (.D(main_bus), .en(MAR_in), .clk(clk), .Q(MAR_value), .clr(in_1));
  assign ALU_value = decoder_1_out0 ? adder_1_out : 8'bz;  // Controlled_Buffer controlled_buffer_7
  Adder adder_1 (.a(AR_value), .b(BR_value), .out(adder_1_out), .cout(ALU_value_carry));  // open: cin
  assign ALU_value = decoder_1_out1 ? subtractor_1_out : 8'bz;  // Controlled_Buffer controlled_buffer_8
  Subtractor subtractor_1 (.a(AR_value), .b(BR_value), .out(subtractor_1_out));  // open: bin, bout
  Decoder #(.enable("false")) decoder_1 (.out0(decoder_1_out0), .out1(decoder_1_out1), .sel(ALU_instruction));
  // Probe on PC_value
  // Probe on AR_value
  // Probe on ALU_value
  // Probe on BR_value
  // Probe on DR_value
  J_K_Flip_Flop #(.trigger("falling")) j_k_ff_1 (
    .J(1'b1), .K(1'b1), .clk(clk), .Q(RAM_out), .Qn(MAR_in), .reset(stepper_reset));  // open: preset
  RAM #(.enables("line")) Memory (.addr(MAR_value), .we(RAM_in), .clk(clk), .din(main_bus), .dout(RAM_value));
  Counter #(.max('h1), .trigger("falling"), .width(1)) counter_1 (
    .load(stepper_reset), .D(1'b0), .Q(out_2), .clk(clk), .clr(in_1));  // open: count, carry, up
  Counter Program_Counter (
    .load(PC_in), .D(main_bus), .count(MAR_in), .Q(PC_value), .clk(clk), .clr(in_1));  // open: carry, up
  Register #(.trigger("falling"), .width(4)) register_1 (
    .D(IR_value[7:4]), .en(1'b1), .clk(clk), .Q(register_1_q), .clr(in_1));
  Counter #(.max('h7), .trigger("falling"), .width(3)) counter_2 (
    .load(stepper_reset), .D(3'b000), .Q(counter_2_q), .clk(clk), .clr(in_1));  // open: count, carry, up
  ROM #(.addrWidth(7), .dataWidth(16)) rom_1 ();  // open: addr, data

  // Other names for the same wires on the sheet: PC_en = MAR_in; PC_out = MAR_in; opcode[3:0] = IR_value[7:4];
  //   reset = in_1

  // Notes on the sheet:
  //   0/1 = add/subtract
  //   ALU
  //   Clock
  //   Instruction Set:
  //   LDA [0001] [memory address] - loads value at memory address to register A
  //   LDB [0010] [memory address] - loads value at memory address to register B
  //   ADD [0011] [memory address] - add AR and BR and stores result to memory address
  //   SUB [0100] [memory address] - subtract BR from AR and stores result to memory address
  //   OUT [0101] [memory address] - loads value at memory address to Display register to display
  //   HALT [1111]                             - halts computer by disabling clock
  //   Control Unit
  //   contents of rom_1 (hex, n*v repeats v):
  //   8060 7*0 88 124 a 8060 4*0 88 424 a 8060 4*0 88 2014 a 8060 4*0 88 3014 a 8060 4*0 88 4024 a 8060
  //   1
  //   2
  //   4
  //   8
  //   1
  //   2
  //   4
  //   8
  //   1
  //   2
  //   4
  //   8
  //   1
  //   2
  //   4
  //   8
endmodule
