// Logisim project digital_display.circ as structural Verilog: 1 circuit, main circuit main
module main (
  input  [7:0] in_1,
  input  [7:0] in_2,
  input  [3:0] in_3,
  output [3:0] out_4,
  output [3:0] out_5,
  output [3:0] out_6
);

  wire clock_1_out, decoder_1_out0, decoder_1_out1, decoder_1_out2, decoder_1_out3;
  wire [1:0] j_k_ff_1_q;
  wire [3:0] controlled_buffer_1_out, controlled_buffer_1_out_2, controlled_buffer_2_out,
       controlled_buffer_2_out_2, controlled_buffer_3_out, controlled_buffer_3_out_2,
       controlled_buffer_4_out, controlled_buffer_4_out_2;
  wire [7:0] rom_1_data;

  J_K_Flip_Flop #(.trigger("falling")) j_k_ff_1 (
    .J(1'b1), .K(1'b1), .clk(clock_1_out), .Q(j_k_ff_1_q[0]));  // open: Qn, preset, reset
  Clock clock_1 (.out(clock_1_out));
  _7_Segment_Display u_7_segment_display_1 ();  // open: g, f, a, b, e, d, c, dp
  // BCD_to_7_Segment_decoder bcd_to_7_segment_decoder_1: pin names not known; wires that end beside it: in_3
  J_K_Flip_Flop #(.trigger("falling")) j_k_ff_2 (
    .J(1'b1), .K(1'b1), .clk(j_k_ff_1_q[0]), .Q(j_k_ff_1_q[1]));  // open: Qn, preset, reset
  Decoder #(.select(2)) decoder_1 (
    .out0(decoder_1_out0), .out1(decoder_1_out1), .out2(decoder_1_out2), .out3(decoder_1_out3),
    .sel(j_k_ff_1_q));  // open: en
  ROM #(.addrWidth(10)) rom_1 (.addr({j_k_ff_1_q, in_1}), .data(rom_1_data));
  // Binairy_to_BCD_converter #(.binvalue(8)) binairy_to_bcd_converter_1: pin names not known; wires that end beside it: in_2, out_4, out_5, out_6
  assign {controlled_buffer_1_out_2, controlled_buffer_1_out} = decoder_1_out3 ? rom_1_data : 8'bz;  // Controlled_Buffer controlled_buffer_1
  assign {controlled_buffer_2_out_2, controlled_buffer_2_out} = decoder_1_out2 ? rom_1_data : 8'bz;  // Controlled_Buffer controlled_buffer_2
  _7_Segment_Display u_7_segment_display_2 (
    .g(controlled_buffer_1_out_2[3]), .f(controlled_buffer_1_out_2[2]), .a(controlled_buffer_1_out_2[1]),
    .b(controlled_buffer_1_out_2[0]), .e(controlled_buffer_1_out[3]), .d(controlled_buffer_1_out[2]),
    .c(controlled_buffer_1_out[1]), .dp(controlled_buffer_1_out[0]));
  assign {controlled_buffer_3_out_2, controlled_buffer_3_out} = decoder_1_out1 ? rom_1_data : 8'bz;  // Controlled_Buffer controlled_buffer_3
  assign {controlled_buffer_4_out_2, controlled_buffer_4_out} = decoder_1_out0 ? rom_1_data : 8'bz;  // Controlled_Buffer controlled_buffer_4
  _7_Segment_Display u_7_segment_display_3 (
    .g(controlled_buffer_2_out_2[3]), .f(controlled_buffer_2_out_2[2]), .a(controlled_buffer_2_out_2[1]),
    .b(controlled_buffer_2_out_2[0]), .e(controlled_buffer_2_out[3]), .d(controlled_buffer_2_out[2]),
    .c(controlled_buffer_2_out[1]), .dp(controlled_buffer_2_out[0]));
  _7_Segment_Display u_7_segment_display_4 (
    .g(controlled_buffer_3_out_2[3]), .f(controlled_buffer_3_out_2[2]), .a(controlled_buffer_3_out_2[1]),
    .b(controlled_buffer_3_out_2[0]), .e(controlled_buffer_3_out[3]), .d(controlled_buffer_3_out[2]),
    .c(controlled_buffer_3_out[1]), .dp(controlled_buffer_3_out[0]));
  _7_Segment_Display u_7_segment_display_5 (
    .g(controlled_buffer_4_out_2[3]), .f(controlled_buffer_4_out_2[2]), .a(controlled_buffer_4_out_2[1]),
    .b(controlled_buffer_4_out_2[0]), .e(controlled_buffer_4_out[3]), .d(controlled_buffer_4_out[2]),
    .c(controlled_buffer_4_out[1]), .dp(controlled_buffer_4_out[0]));

  // Notes on the sheet:
  //   contents of rom_1 (hex, n*v repeats v):
  //   7e 12 bc b6 d2 e6 ee 32 fe f6 7e 12 bc b6 d2 e6 ee 32 fe f6 7e 12 bc b6 d2 e6 ee 32 fe f6 7e 12 bc
  //   b6 d2 e6 ee 32 fe f6 7e 12 bc b6 d2 e6 ee 32 fe f6 7e 12 bc b6 d2 e6 ee 32 fe f6 7e 12 bc b6 d2 e6
  //   ee 32 fe f6 7e 12 bc b6 d2 e6 ee 32 fe f6 7e 12 bc b6 d2 e6 ee 32 fe f6 7e 12 bc b6 d2 e6 ee 32 fe
  //   f6 7e 12 bc b6 d2 e6 ee 32 fe f6 7e 12 bc b6 d2 e6 ee 32 fe f6 7e 12 bc b6 d2 e6 ee 32 fe f6 7e 12
  //   bc b6 d2 e6 ee 32 fe f6 7e 12 bc b6 d2 e6 ee 32 fe f6 7e 12 bc b6 d2 e6 ee 32 fe f6 7e 12 bc b6 d2
  //   e6 ee 32 fe f6 7e 12 bc b6 d2 e6 ee 32 fe f6 7e 12 bc b6 d2 e6 ee 32 fe f6 7e 12 bc b6 d2 e6 ee 32
  //   fe f6 7e 12 bc b6 d2 e6 ee 32 fe f6 7e 12 bc b6 d2 e6 ee 32 fe f6 7e 12 bc b6 d2 e6 ee 32 fe f6 7e
  //   12 bc b6 d2 e6 ee 32 fe f6 7e 12 bc b6 d2 e6 ee 32 fe f6 7e 12 bc b6 d2 e6 10*0 10*12 10*bc 10*b6
  //   10*d2 10*e6 10*ee 10*32 10*fe 10*f6 10*7e 10*12 10*bc 10*b6 10*d2 10*e6 10*ee 10*32 10*fe 10*f6
  //   10*7e 10*12 10*bc 10*b6 10*d2 6*e6 99*0 100*12 57*bc
endmodule
